# Fritzing sketch WateringMachine_ESP8266 (saved by Fritzing 0.9.3b)
breadboards: 2

parts:
  Part2 = Adafruit ADS1115 16Bit I2C ADC [part_number="Adafruit #1085"]
  NodeMCU_v2 = NodeMCU v3 LoLin [part_number=ESP8266]
  Part3 = KY-019 5V Relay Module [package="Breakout board"]
  Part4 = KY-019 5V Relay Module [package="Breakout board"]
  Power_plug2 = Power plug
  Part5 = VERTER 5V USB Buck-Boost
  Part6 = Soil Moisture Sensor
  Part7 = Soil Moisture Sensor
  Part8 = VERTER 5V USB Buck-Boost
  LED2 = LEDs [package=led10mm]
  LED3 = LEDs [package=led10mm]
  M2 = DC Motor  # not connected
  Stepdown_Voltage1 = Polulu Stepdown Voltage [part_number=D24V25F3,D24V25F5]
  M3 = DC Motor

nets:
  N1: Part2.AIN1, Part7.SIG
  N2: Part2.AIN0, Part6.SIG
  N3: Part2.SDA, NodeMCU_v2.D2
  N4: Part2.SCL, NodeMCU_v2.D1
  GND: Part2.GND, NodeMCU_v2.GND#6, NodeMCU_v2.GND#13, NodeMCU_v2.GND#16, NodeMCU_v2.GND#33, Part3.-, Part4.-, Part6.GND, Part7.GND, Stepdown_Voltage1.GND#3
  VCC: Part2.VDD, NodeMCU_v2.3V3, Part3.+, Part4.+, Part6.VCC, Part7.VCC
  N5: NodeMCU_v2.D5, Part3.S
  N6: NodeMCU_v2.D7, Part4.S
  N7: NodeMCU_v2.VIN, Stepdown_Voltage1.VOut
  VCC_2: Part3.Common, Part4.Common, Power_plug2.VCC, Stepdown_Voltage1.VIn
  N8: Part3.NO, M3.pin_1
  VIN: Part4.NO, Part5.VIN, Part8.VIN
  GND_2: Power_plug2.GND, Part5.GND, Part8.GND, LED2.A, LED3.A, Stepdown_Voltage1.GND#2, M3.pin_2
  N9: Part5.5.0V, LED2.C
  N10: Part8.5.0V, LED3.C

custom parts:
  Adafruit ADS1115 16Bit I2C ADC: For microcontrollers without an analog-to-digital converter or when you want a higher-precision ADC, the ADS1115 provides 16-bit precision at 860 samples/second over I2C. The chip can be configured as 4 single-ended input channels, or two differential channels. As a nice bonus, it even includes a programmable gain amplifier, up to x16, to help boost up smaller single/differential signals to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
  NodeMCU v3 LoLin: NodeMCU v3 LoLin NodeMCU (http://www.nodemcu.com/) is an open source IoT platform. It includes firmware (https://nodemcu-build.com/) which runs on the ESP8266 Wi-Fi SoC from Espressif Systems, and hardware which is based on the ESP-12E module. The term "NodeMCU" by default refers to the firmware rather than the dev kits. The firmware uses the Lua scripting language. It is based on the eLua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
  KY-019 5V Relay Module: KY-019 5V Relay module, used to control AC circuits.
  VERTER 5V USB Buck-Boost: VERTER can take battery voltages from 3-12VDC and output a nice 5V DC, which makes it a perfect universal power supply for your portable project! Where Verter really shines is when you have a battery or power range that can fluctuate a lot, or you don't know what you'll end up using.
  Polulu Stepdown Voltage: Polulu Stepdown Voltage 3V3 or 5V, 2.5A
